# Fritzing sketch MicroEdition-v3 (saved by Fritzing 0.9.1b)
breadboards: 2

parts:
  Composant1 = Arduino Uno (Rev3)
  RHT1 = Humidity and Temperature Sensor RHT03
  R1 = PHOTOCELL [package=photocell]
  V1 = DC Power [voltage=12V]  # not connected
  LED1 = LEDs [package=led10mm]
  R2 = Resistor [tolerance=±5% resistance=10k package=THT]
  R3 = Resistor [tolerance=±5% resistance=10k package=THT]
  R5 = TRIMPOT [package=3362u-2]
  U2 = LCD-16X2 [package=lcd-16x2]
  Composant2 = Real Time Clock Module - DS1307 RTC Breakout Board
  Power_plug1 = Power plug  # not connected
  Power_plug2 = Power plug
  M1 = DC Motor  # not connected

nets:
  N1: Composant1.A1, R1.P$2, R2.Pin_1
  N2: Composant1.D11_PWM/MOSI, U2.E
  N3: Composant1.D12/MISO, U2.RS
  N4: Composant1.A4/SDA, Composant2.SDA
  N5: Composant1.A5/SCL, Composant2.SCL
  N6: Composant1.D2, U2.DB7
  N7: Composant1.D3_PWM, U2.DB6
  N8: Composant1.D4, U2.DB5
  N9: Composant1.D5_PWM, U2.DB4
  N10: Composant1.D7, RHT1.Data-signal, R3.Pin_0
  5V: Composant1.5V, RHT1.Vcc, R1.P$1, R3.Pin_1, R5.CW, U2.VDD, U2.A, Composant2.5V
  GND: Composant1.GND, RHT1.GND_2, R2.Pin_0, R5.CCW, U2.VSS, U2.R_W, U2.K, Composant2.GND
  N11: LED1.C, Power_plug2.GND
  N12: R5.WIPER, U2.VO

notes:
  Relay Module
  2 channels
  Voltage
  regulator
  12V
  5V Output
  12V Output
  Power Supply
  220v --> 12V & 5V
  Water Pump
  LED Light
